# Fritzing sketch ArmShem (saved by Fritzing 0.9.3b)
breadboards: 1

parts:
  X1 = X113647 Stepper Driver Board [package=board]
  X2 = X113647 Stepper Driver Board [package=board]
  X3 = X113647 Stepper Driver Board [package=board]
  MOTOR1 = 28BYJ-48 Stepper Motor
  MOTOR2 = 28BYJ-48 Stepper Motor
  MOTOR3 = 28BYJ-48 Stepper Motor
  Часть1 = Arduino Uno (Rev3)
  J1 = Basic Servo

nets:
  N1: X1.IN1, Часть1.D6_PWM
  N2: X1.IN2, Часть1.D7
  N3: X1.IN3, Часть1.D8
  N4: X1.IN4, Часть1.D9_PWM
  GND: X1.GND, X2.GND, X3.GND, Часть1.GND, J1.gnd
  5V: X1.+V, X2.+V, X3.+V, Часть1.5V, J1.vcc
  N5: X1.BLUE, MOTOR2.BLUE
  N6: X1.PINK, MOTOR2.PINK
  N7: X1.YELLOW, MOTOR2.YELLOW
  N8: X1.ORANGE, MOTOR2.ORANGE
  N9: X1.RED, MOTOR2.RED
  N10: X2.IN1, Часть1.D2
  N11: X2.IN2, Часть1.D3_PWM
  N12: X2.IN3, Часть1.D4
  N13: X2.IN4, Часть1.D5_PWM
  N14: X2.BLUE, MOTOR3.BLUE
  N15: X2.PINK, MOTOR3.PINK
  N16: X2.YELLOW, MOTOR3.YELLOW
  N17: X2.ORANGE, MOTOR3.ORANGE
  N18: X2.RED, MOTOR3.RED
  N19: X3.IN1, Часть1.D10_PWM/SS
  N20: X3.IN2, Часть1.D11_PWM/MOSI
  N21: X3.IN3, Часть1.D12/MISO
  N22: X3.IN4, Часть1.D13/SCK
  N23: X3.BLUE, MOTOR1.BLUE
  N24: X3.PINK, MOTOR1.PINK
  N25: X3.YELLOW, MOTOR1.YELLOW
  N26: X3.ORANGE, MOTOR1.ORANGE
  N27: X3.RED, MOTOR1.RED
  N28: Часть1.A5/SCL, J1.pulse

custom parts:
  X113647 Stepper Driver Board: A common stepper motor driver board based on ULN2003APG darlington array
